# Fritzing sketch schematic (saved by Fritzing 0.9.3b)

parts:
  U1 = NEO 6M GPS
  SD_card_module1 = SD Card Module
  Part2 = LCD1602-I2C
  U2 = NodeMCU V3.0

nets:
  N1: U1.RXD, U2.D4
  N2: U1.TXD, U2.D3
  GND: U1.GND, Part2.GND, U2.GND
  VCC: U1.VCC, U2.3V3
  N3: SD_card_module1.CS, U2.D8
  N4: SD_card_module1.MOSI, U2.D7
  N5: SD_card_module1.SCK, U2.D5
  N6: SD_card_module1.MISO, U2.D6
  N7: Part2.VCC, U2.VU
  N8: Part2.SDA, U2.D2
  N9: Part2.SCL, U2.D1

notes:
  N/A
  RXD
  TXD
  GND
  3.3v

custom parts:
  NEO 6M GPS: uSD module
  SD Card Module: SD Card Module Slot Socket Reader For Arduino ARM MCU
  LCD1602-I2C: A standard character display, usually with 2x16 characters. Comes in many colors with LCM1602 IIC attached.
  NodeMCU V3.0: ESP8266 based NodeMCU
